# Fritzing sketch nodemcu_botao_led (saved by Fritzing 0.9.3b)
breadboards: 1

parts:
  U1 = NodeMCU V3.0
  LED1 = smd LED [color="Red (633nm)" package="0805 [SMD]"]  # not connected
  S2 = Pushbutton [package="[THT]"]
  R1 = Resistor [tolerance=±5% resistance=220 package="2010 [SMD]"]

nets:
  N1: U1.D2, S2.Pin_3, S2.Pin_4, R1.Pin_1
  N2: U1.3V3, S2.Pin_1, S2.Pin_2
  N3: U1.GND, R1.Pin_0

custom parts:
  NodeMCU V3.0: ESP8266 based NodeMCU
