# Fritzing sketch nodemcu_luz_emergencia (saved by Fritzing 0.9.3b)
breadboards: 1

parts:
  U1 = NodeMCU V3.0
  LED1 = smd LED [color="Red (633nm)" package="0805 [SMD]"]  # not connected
  R1 = Resistor [tolerance=±5% resistance=220 package="2010 [SMD]"]
  R2 = Photocell (LDR) [package=THT]

nets:
  N1: U1.3V3, R2.pin_1
  N2: U1.GND, R1.Pin_1
  N3: U1.A0, R1.Pin_0, R2.pin_0

custom parts:
  NodeMCU V3.0: ESP8266 based NodeMCU
